// Logisim project Control Unit.circ as structural Verilog
module Control_Unit_2 (
  input  Start,
  input  Fetched,
  input  Halt_Instruction,
  input  Ejecutada,
  input  in_5,
  input  in_6,
  input  in_7,
  input  in_8,
  output out_9,
  output CS,
  output out_11
);

  wire Chip_Select, Clock, d_ff_1_q, demultiplexer_1_out0, demultiplexer_1_out1, demultiplexer_2_out0,
       demultiplexer_3_out0, demultiplexer_3_out1, demultiplexer_4_out0, demultiplexer_5_out0,
       demultiplexer_5_out1, demultiplexer_6_out0, demultiplexer_6_out1, demultiplexer_7_out0,
       demultiplexer_7_out1, Execute, Execute_Finished, Fecth_Finished, Fetch, Fetched_t, Halt,
       Idle_Finished, or_3_out, or_5_out, or_7_out, Reset, undriven, undriven_2;

  Demultiplexer #(.enable("false")) demultiplexer_1 (
    .out0(demultiplexer_1_out0), .out1(demultiplexer_1_out1), .in(demultiplexer_1_out0), .sel(Start));
  Demultiplexer #(.enable("false")) demultiplexer_2 (
    .out0(demultiplexer_2_out0), .out1(Idle_Finished), .in(d_ff_1_q), .sel(Reset));
  D_Flip_Flop d_ff_1 (.clk(Clock), .D(demultiplexer_2_out0), .Q(d_ff_1_q), .preset(Reset));  // open: Qn, en, reset
  or or_1 (out_9, demultiplexer_3_out0, demultiplexer_6_out1, demultiplexer_1_out1);
  or or_2 (Chip_Select, Fetch, Execute);
  or or_3 (or_3_out, demultiplexer_4_out0, Execute_Finished, Idle_Finished);
  Demultiplexer #(.enable("false")) demultiplexer_3 (
    .out0(demultiplexer_3_out0), .out1(demultiplexer_3_out1), .in(out_9));  // open: sel
  D_Flip_Flop d_ff_2 (.clk(Clock), .D(or_3_out), .Q(Fetch), .preset(Reset));  // open: Qn, en, reset
  Demultiplexer #(.enable("false")) demultiplexer_4 (
    .out0(demultiplexer_4_out0), .out1(Fecth_Finished), .in(Fetch), .sel(Fetched_t));
  Demultiplexer #(.enable("false")) demultiplexer_5 (
    .out0(demultiplexer_5_out0), .out1(demultiplexer_5_out1), .in(demultiplexer_3_out1),
    .sel(Halt_Instruction));
  or or_4 (out_11, demultiplexer_6_out0, demultiplexer_5_out0);
  or or_5 (or_5_out, demultiplexer_7_out0, Fecth_Finished);
  Demultiplexer demultiplexer_6 (
    .out0(demultiplexer_6_out0), .out1(demultiplexer_6_out1), .in(out_11), .en(Ejecutada));  // open: sel
  D_Flip_Flop d_ff_3 (.clk(Clock), .D(or_5_out), .Q(Execute), .preset(Reset));  // open: Qn, en, reset
  Demultiplexer #(.enable("false")) demultiplexer_7 (
    .out0(demultiplexer_7_out0), .out1(demultiplexer_7_out1), .in(Execute));  // open: sel
  Demultiplexer #(.enable("false")) demultiplexer_8 (
    .out0(Execute_Finished), .out1(in_8), .in(demultiplexer_7_out1), .sel(Halt));
  or or_6 (CS, undriven, undriven_2);
  or or_7 (or_7_out, in_8, in_8);
  D_Flip_Flop d_ff_4 (.clk(Clock), .D(or_7_out), .Q(in_8), .preset(Reset));  // open: Qn, en, reset

  // Other names for the same wires on the sheet: Clock_cambiar_etiqueta_al_nombre_real_del_reloj_que_controla_el_funcionamiento_general = in_5;
  //   End = in_8; Fetched_cambiar_x_nombre_de_la_entrada_que_indica_que_ya_se_tiene_la_instruccion = in_6;
  //   Reset_cambiar_etiqueta_al_nombre_real_que_se_reciba = in_7

  // Notes on the sheet:
  //   Iddle
  //   Inputs
  //   Outputs
  //   Idle
  //   Capturar Instruccion
  //   Fetch
  //   Esquema de guia
  //   Execute
  //   Execute
  //   Captura Instruccion
  //   Ejecuta Instruccion 
  //   End
  //   End
endmodule
